# Fritzing sketch helmlight (saved by Fritzing 0.9.2b)
breadboards: 1

parts:
  C1 = Electrolytic Capacitor [capacitance=22µF voltage=16V package="100 mil [THT, electrolytic]"]
  ESP-8266_ESP-03 = mystery part, 14 pins [chip_label="ESP-8266 ESP-03" part_number="ESP-8266 ESP-03"]
  VCC1 = Battery
  R1 = Resistor [tolerance=±5% resistance=10k package=THT]
  R2 = Resistor [tolerance=±5% resistance=220 package=THT]
  LED1 = LED - 5mm [color="Red (633nm)" package="5 mm [THT]"]
  Part1 = Arduino Uno (Rev3)  # not connected
  C2 = Electrolytic Capacitor [capacitance=1mF voltage=16V package="100 mil [THT, electrolytic]"]  # not connected
  R3 = Resistor [tolerance=±5% resistance=470 package=THT]  # not connected

nets:
  N1: C1.-, ESP-8266_ESP-03.pin1, VCC1.+, R1.Pin_0
  N2: C1.+, ESP-8266_ESP-03.pin8, VCC1.-, LED1.cathode
  N3: ESP-8266_ESP-03.pin7, R2.Pin_1
  N4: ESP-8266_ESP-03.pin13, R1.Pin_1
  N5: R2.Pin_0, LED1.anode
